# Fritzing sketch 고정밀 ph 측정기-bread (saved by Fritzing 0.9.3b)

parts:
  Adafruit_ADS1115 = Adafruit ADS1115 16Bit I2C ADC [part_number="Adafruit #1085"]
  아두이노_나노 = Arduino Nano (Rev3.0)
  DS18B20_온도센서 = DS18B20 1-Wire Temperature Sensor Probe Cable
  Star_Grount_Point = STARBOARD_GND [package=starboard_ground_small2]
  HC-06 = Bluetooth HC-06u [package=THT]
  R2 = Resistor [tolerance=±5% resistance=4.7k package=THT]
  L298N1 = L298N DC motor driver
  L298N2 = L298N DC motor driver
  L298N3 = L298N DC motor driver
  R5 = Resistor [tolerance=±20% resistance=20k package=THT]
  R4 = Resistor [tolerance=±5% resistance=10k package=THT]
  12V_DC_잭 = 2.1mm Barrel Jack with Terminal Block
  참조물_에어_공급 = 6V Mini Solenoid Valve 3-Way (SZH-GNP114)
  연동_펌프 = Peristaltic Dosing Pump 12V (NKP-DC-B06B)
  PUMP2 = Peristaltic Dosing Pump 12V (NKP-DC-B06B)
  PUMP3 = Peristaltic Dosing Pump 12V (NKP-DC-B06B)
  PUMP4 = Peristaltic Dosing Pump 12V (NKP-DC-B06B)
  수조물_에어_공급 = 6V Mini Solenoid Valve 3-Way (SZH-GNP114)
  12V_->_5V = 5V Fixed DC-DC Buck Converter 3A (SZH-PWSD-016)
  12V_->_6V = FND XL4015 DC-DC Buck Converter 5A (SZH-PWSDF-036)
  DC_모터_PWM_속도_조절 = PWM DC Motor Speed Controller 2A (SZH-MSC-009)
  U2 = PWM DC Motor Speed Controller 2A (SZH-MSC-009)
  U3 = PWM DC Motor Speed Controller 2A (SZH-MSC-009)
  U4 = PWM DC Motor Speed Controller 2A (SZH-MSC-009)
  C1 = Ceramic Capacitor [capacitance="100 nF" package="1206 [SMD, multilayer]"]
  C2 = Ceramic Capacitor [capacitance="100 nF" package="1206 [SMD, multilayer]"]
  C3 = Ceramic Capacitor [capacitance="100 nF" package="1206 [SMD, multilayer]"]
  R6 = Resistor [tolerance=±20% resistance=330 package=THT]
  C4 = Ceramic Capacitor [capacitance="100 nF" package="1206 [SMD, multilayer]"]
  PROBE1 = Gravity pH Probe Laboratory Grade (SEN0161-V2)
  DFRobot_SEN0161_pH_미터_V2 = Gravity pH Meter V2 Signal Board (SEN0161-V2)

nets:
  N1: Adafruit_ADS1115.AIN0, R6.Pin_1, C4.1
  N2: Adafruit_ADS1115.SDA, 아두이노_나노.A4
  N3: Adafruit_ADS1115.SCL, 아두이노_나노.A5
  GND: Adafruit_ADS1115.GND, 아두이노_나노.GND, DS18B20_온도센서.GND, Star_Grount_Point.MOUNT, HC-06.GND, L298N1.GND, L298N2.GND, L298N3.GND, R5.Pin_0, 12V_DC_잭.NEG, 12V_->_5V.IN-, 12V_->_5V.OUT-, 12V_->_6V.IN-, 12V_->_6V.OUT+, C1.0, C2.1, C3.1, C4.0, DFRobot_SEN0161_pH_미터_V2.GND
  VDD: Adafruit_ADS1115.VDD, 아두이노_나노.5V, DS18B20_온도센서.VDD, HC-06.VCC, R2.Pin_1, L298N1.5V#7, L298N2.5V#7, L298N3.5V#7, 12V_->_5V.OUT+, C1.1, C2.0, C3.0, DFRobot_SEN0161_pH_미터_V2.V+
  N4: 아두이노_나노.D1/TX, R4.Pin_0
  N5: 아두이노_나노.D0/RX, HC-06.TXD
  N6: 아두이노_나노.D4, L298N1.IN4
  N7: 아두이노_나노.D5, L298N1.IN3
  N8: 아두이노_나노.D6, L298N1.IN2
  N9: 아두이노_나노.D7, L298N1.IN1
  N10: 아두이노_나노.D8, L298N2.IN4
  N11: 아두이노_나노.D9, L298N2.IN3
  N12: 아두이노_나노.D10, L298N2.IN2
  N13: 아두이노_나노.D11/MOSI, L298N2.IN1
  N14: 아두이노_나노.D12/MISO, L298N3.IN3
  N15: 아두이노_나노.A0, DS18B20_온도센서.DQ, R2.Pin_0
  N16: 아두이노_나노.D13/SCK, L298N3.IN1
  N17: HC-06.RXD, R5.Pin_1, R4.Pin_1
  N18: L298N1.OUT1, U2.Power-
  N19: L298N1.OUT2, U2.Power+
  N20: L298N1.OUT3, DC_모터_PWM_속도_조절.Power+
  N21: L298N1.OUT4, DC_모터_PWM_속도_조절.Power-
  12V: L298N1.12V, L298N2.12V, 12V_DC_잭.POS, 12V_->_5V.IN+, 12V_->_6V.IN+
  N22: L298N1.5V#9, L298N1.ENA
  N23: L298N1.5V#10, L298N1.ENB
  N24: L298N2.OUT1, U4.Power-
  N25: L298N2.OUT2, U4.Power+
  N26: L298N2.OUT3, U3.Power+
  N27: L298N2.OUT4, U3.Power-
  N28: L298N2.5V#9, L298N2.ENA
  N29: L298N2.5V#10, L298N2.ENB
  N30: L298N3.OUT1, 수조물_에어_공급.GND
  N31: L298N3.OUT2, 수조물_에어_공급.VCC
  N32: L298N3.OUT3, 참조물_에어_공급.VCC
  N33: L298N3.OUT4, 참조물_에어_공급.GND
  N34: L298N3.12V, 12V_->_6V.OUT-
  N35: L298N3.5V#9, L298N3.ENA
  N36: L298N3.5V#10, L298N3.ENB
  N37: 연동_펌프.VCC+, DC_모터_PWM_속도_조절.Motor+
  N38: 연동_펌프.GND-, DC_모터_PWM_속도_조절.Motor-
  N39: PUMP2.VCC+, U2.Motor+
  N40: PUMP2.GND-, U2.Motor-
  N41: PUMP3.VCC+, U3.Motor+
  N42: PUMP3.GND-, U3.Motor-
  N43: PUMP4.VCC+, U4.Motor+
  N44: PUMP4.GND-, U4.Motor-
  N45: R6.Pin_0, DFRobot_SEN0161_pH_미터_V2.A
  N46: PROBE1.BNC-, DFRobot_SEN0161_pH_미터_V2.BNC

notes:
  Star Ground Point
  (AGND-회색 & DGND-검은색 결합점)
  DGND - 회색, AGND - 검정
  결합점,
  전원 GND

custom parts:
  Adafruit ADS1115 16Bit I2C ADC: For microcontrollers without an analog-to-digital converter or when you want a higher-precision ADC, the ADS1115 provides 16-bit precision at 860 samples/second over I2C. The chip can be configured as 4 single-ended input channels, or two differential channels. As a nice bonus, it even includes a programmable gain amplifier, up to x16, to help boost up smaller single/differential signals to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
  Bluetooth HC-06u: Bluetooth HC-06 - face up, pins down 16.5mm x 37.5mm PCB
  L298N DC motor driver: 2x DC motor driver with 78M05 positive voltage regulator (7..35 V) L298N: max 46 V, 2 A Set 5 V Enable jumper to enable 5 V regultor (needed for the L298N) and +5 V output at screw terminal or supply external +5 V at screw terminal Set ENA and/or ENB to +5 V to enable motor permanently or supply ENA and/or ENB with PWM signal IN1 and IN2 set rotation directory for motor A (OUT1/OUT2) IN2 and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
  6V Mini Solenoid Valve 3-Way (SZH-GNP114): 6V Mini 3-Way Solenoid Valve SZH-GNP114 (ZHY-0519). OFF: air flows IN-top to Port-A-left. ON: air flows IN-top to Port-B-right. 2-pin JST connector.
  Peristaltic Dosing Pump 12V (NKP-DC-B06B): Kamoer NKP-DC-B06B Peristaltic Dosing Pump. 12V DC / 0.15A. Flow 5.2~90ml/min. BPT silicone tube 2x4mm. 3-wheel. For Arduino aquarium/lab DIY. Size: 67x41x55mm.
  5V Fixed DC-DC Buck Converter 3A (SZH-PWSD-016): 5V Fixed Output Step-Down DC-DC Converter 3A. Input 7V-26V, Output 5V/3A, max 96% efficiency. SZH-PWSD-016.
  FND XL4015 DC-DC Buck Converter 5A (SZH-PWSDF-036): FND Voltage Display XL4015 Step-Down DC-DC 5A Adjustable Converter SZH-PWSDF-036. Input 4V-38V, Output 1.25V-35V/5A. Built-in FND voltage display.
  PWM DC Motor Speed Controller 2A (SZH-MSC-009): PWM DC Motor Speed Controller 2A SZH-MSC-009. Input DC 1.8V-15V, Max 30W/2A. Duty cycle 0-100% via potentiometer knob.
  Gravity pH Probe Laboratory Grade (SEN0161-V2): DFRobot Gravity Analog pH Probe Laboratory Grade. SEN0161-V2. Range 0-14 pH, 5-60°C, BNC connector, 100cm cable. Connect to Signal Board BNC port.
  Gravity pH Meter V2 Signal Board (SEN0161-V2): DFRobot Gravity Analog pH Sensor Signal Conversion Board V2. SEN0161-V2. Supply 3.3-5.5V, Output 0-3V, BNC probe connector, Gravity PH2.0-3P signal connector.
